# Fritzing sketch AccessControlSystemMega (saved by Fritzing 0.9.3b)
breadboards: 1

parts:
  Part1 = Arduino Mega 2560 (Rev3)
  Part2 = RFID-RC522-v3
  R1 = Resistor [tolerance=±5% resistance=220 package=THT]
  R3 = Resistor [tolerance=±5% resistance=220 package=THT]
  R2 = Resistor [tolerance=±5% resistance=220 package=THT]
  J1 = Piezo Speaker
  LED1 = LED - 5mm [color="Green (555nm)" package="5 mm [THT]"]
  LED2 = LED - 5mm [color="Blue (430nm)" package="5 mm [THT]"]
  LED3 = LED - 5mm [color="Red (633nm)" package="5 mm [THT]"]

nets:
  3V3: Part1.3V3, Part2.3.3V
  GND: Part1.GND, Part2.GND, J1.pin1, LED1.cathode, LED2.cathode, LED3.cathode
  N1: Part1.D4_PWM, J1.pin2
  N2: Part1.D5_PWM, Part2.RST
  N3: Part1.D6_PWM, R2.Pin_0
  N4: Part1.D7_PWM, R3.Pin_0
  N5: Part1.D50, Part2.MISO
  N6: Part1.D51, Part2.MOSI
  N7: Part1.D52, Part2.SCK
  N8: Part1.D53, Part2.SDA
  N9: R1.Pin_1, LED3.anode
  N10: R3.Pin_1, LED2.anode
  N11: R2.Pin_1, LED1.anode

custom parts:
  RFID-RC522-v3: A simple China made RFID-RC522 Reader (6x4 cm); do check the pin labels, as this is a MFRC522 based clone.
