# Fritzing sketch AccessControlSystemMegaKeypad (saved by Fritzing 0.9.3b)
breadboards: 1

parts:
  Part1 = Arduino Mega 2560 (Rev3)
  Part2 = RFID-RC522-v3
  R1 = Resistor [tolerance=±5% resistance=220 package=THT]
  R3 = Resistor [tolerance=±5% resistance=220 package=THT]
  R2 = Resistor [tolerance=±5% resistance=220 package=THT]
  J1 = Piezo Speaker
  Keypad4x1 = Keypad Membran 4x4
  LED1 = LED - 5mm [color="Green (555nm)" package="5 mm [THT]"]
  LED2 = LED - 5mm [color="Blue (430nm)" package="5 mm [THT]"]
  LED3 = LED - 5mm [color="Red (633nm)" package="5 mm [THT]"]

nets:
  3V3: Part1.3V3, Part2.3.3V
  GND: Part1.GND, Part2.GND, J1.pin1, LED1.cathode, LED2.cathode, LED3.cathode
  N1: Part1.D4_PWM, J1.pin2
  N2: Part1.D5_PWM, Part2.RST
  N3: Part1.D6_PWM, R2.Pin_0
  N4: Part1.D7_PWM, R3.Pin_0
  N5: Part1.D22, Keypad4x1.Pin1
  N6: Part1.D23, Keypad4x1.Pin2
  N7: Part1.D24, Keypad4x1.Pin3
  N8: Part1.D25, Keypad4x1.Pin4
  N9: Part1.D26, Keypad4x1.Pin5
  N10: Part1.D27, Keypad4x1.Pin6
  N11: Part1.D28, Keypad4x1.Pin7
  N12: Part1.D29, Keypad4x1.Pin8
  N13: Part1.D50, Part2.MISO
  N14: Part1.D51, Part2.MOSI
  N15: Part1.D52, Part2.SCK
  N16: Part1.D53, Part2.SDA
  N17: R1.Pin_1, LED3.anode
  N18: R3.Pin_1, LED2.anode
  N19: R2.Pin_1, LED1.anode

custom parts:
  RFID-RC522-v3: A simple China made RFID-RC522 Reader (6x4 cm); do check the pin labels, as this is a MFRC522 based clone.
  Keypad Membran 4x4: Membrane Keypad 4x4 Matrix
