# Fritzing sketch AccessControlSystemMegaRGBButton (saved by Fritzing 0.9.3b)
breadboards: 1

parts:
  Part1 = Arduino Mega 2560 (Rev3)
  Part2 = RFID-RC522-v3
  R1 = Resistor [tolerance=±5% resistance=220 package=THT]
  LED1 = RGB LED (com. cathode, rgb) [package="5 mm [THT]"]
  R3 = Resistor [tolerance=±5% resistance=220 package=THT]
  R2 = Resistor [tolerance=±5% resistance=220 package=THT]
  R4 = Resistor [tolerance=±5% resistance=220 package=THT]
  J1 = Piezo Speaker
  S1 = Round Pushbutton

nets:
  N1: Part1.D8_PWM, S1.leg1
  3V3: Part1.3V3, Part2.3.3V
  GND: Part1.GND, Part2.GND, R4.Pin_0, J1.pin1, S1.leg0
  N2: Part1.D3_PWM, R1.Pin_0
  N3: Part1.D4_PWM, J1.pin2
  N4: Part1.D5_PWM, Part2.RST
  N5: Part1.D6_PWM, R2.Pin_0
  N6: Part1.D7_PWM, R3.Pin_0
  N7: Part1.D50, Part2.MISO
  N8: Part1.D51, Part2.MOSI
  N9: Part1.D52, Part2.SCK
  N10: Part1.D53, Part2.SDA
  N11: R1.Pin_1, LED1.red_anode
  N12: LED1.common_cathode, R4.Pin_1
  N13: LED1.green_anode, R2.Pin_1
  N14: LED1.blue_anode, R3.Pin_1

custom parts:
  RFID-RC522-v3: A simple China made RFID-RC522 Reader (6x4 cm); do check the pin labels, as this is a MFRC522 based clone.
