# Fritzing sketch RFID Control System Schematic - Mega No Keypad Button RGB (saved by Fritzing 0.9.3b)
breadboards: 1

parts:
  J1 = Piezo Speaker
  Part2 = RFID-RC522-v3
  Part3 = Arduino Mega 2560 (Rev3)
  R4 = Resistor [tolerance=±5% resistance=220 package=THT]
  S1 = Pushbutton [package="[THT]"]
  LED1 = RGB LED (com. cathode, rbg) [package="5 mm [THT]"]

nets:
  GND: J1.pin1, Part2.GND, Part3.GND, R4.Pin_1, LED1.common_cathode
  N1: J1.pin2, Part3.D4_PWM
  N2: Part2.SDA, Part3.D10_PWM
  N3: Part2.SCK, Part3.D13_PWM
  N4: Part2.MOSI, Part3.D11_PWM
  N5: Part2.MISO, Part3.D12_PWM
  N6: Part2.RST, Part3.D9_PWM
  3.3V: Part2.3.3V, Part3.3V3
  N7: Part3.D8_PWM, R4.Pin_0, S1.Pin_1, S1.Pin_2
  N8: Part3.D5_PWM, LED1.red_anode
  N9: Part3.D6_PWM, LED1.blue_anode
  N10: S1.Pin_3, S1.Pin_4

custom parts:
  RFID-RC522-v3: A simple China made RFID-RC522 Reader (6x4 cm); do check the pin labels, as this is a MFRC522 based clone.
