# Fritzing sketch RFID Control System Schematic - Mega No Keypad Button (saved by Fritzing 0.9.3b)
breadboards: 1

parts:
  LED1 = smd LED [color="Blue (470nm)" package="0603 [SMD]"]
  R1 = Resistor [tolerance=±5% resistance=220 package=THT]  # not connected
  LED2 = LED - 5mm [color="Green (555nm)" package="5 mm [THT]"]
  R2 = Resistor [tolerance=±5% resistance=220 package=THT]
  LED3 = LED - 5mm [color="Red (633nm)" package="5 mm [THT]"]
  R3 = Resistor [tolerance=±5% resistance=220 package=THT]
  J1 = Piezo Speaker
  Part2 = RFID-RC522-v3
  Part3 = Arduino Mega 2560 (Rev3)
  R4 = Resistor [tolerance=±5% resistance=220 package=THT]
  S1 = Pushbutton [package="[THT]"]

nets:
  GND: LED1.cathode, LED2.cathode, LED3.cathode, J1.pin1, Part2.GND, Part3.GND, R4.Pin_1
  N1: LED2.anode, R2.Pin_0
  N2: R2.Pin_1, Part3.D3_PWM
  N3: LED3.anode, R3.Pin_0
  N4: R3.Pin_1, Part3.D2_PWM
  N5: J1.pin2, Part3.D4_PWM
  N6: Part2.SDA, Part3.D10_PWM
  N7: Part2.SCK, Part3.D13_PWM
  N8: Part2.MOSI, Part3.D11_PWM
  N9: Part2.MISO, Part3.D12_PWM
  N10: Part2.RST, Part3.D9_PWM
  3.3V: Part2.3.3V, Part3.3V3
  N11: Part3.D8_PWM, R4.Pin_0, S1.Pin_1, S1.Pin_2
  N12: S1.Pin_3, S1.Pin_4

custom parts:
  RFID-RC522-v3: A simple China made RFID-RC522 Reader (6x4 cm); do check the pin labels, as this is a MFRC522 based clone.
