# Fritzing sketch RFID Control System Schematic RGB (saved by Fritzing 0.9.3b)
breadboards: 1

parts:
  Part1 = Arduino Uno (Rev3)
  J1 = Piezo Speaker
  Part2 = RFID-RC522-v3
  LED1 = RGB LED (com. cathode, rbg) [package="5 mm [THT]"]

nets:
  N1: Part1.D9_PWM, Part2.RST
  N2: Part1.D10_PWM/SS, Part2.SDA
  N3: Part1.D11_PWM/MOSI, Part2.MOSI
  N4: Part1.D12/MISO, Part2.MISO
  N5: Part1.D13/SCK, Part2.SCK
  N6: Part1.D4, J1.pin2
  N7: Part1.D5_PWM, LED1.red_anode
  N8: Part1.D6_PWM, LED1.blue_anode
  N9: Part1.D7, LED1.green_anode
  3V3: Part1.3V3, Part2.3.3V
  GND: Part1.GND, J1.pin1, Part2.GND, LED1.common_cathode

custom parts:
  RFID-RC522-v3: A simple China made RFID-RC522 Reader (6x4 cm); do check the pin labels, as this is a MFRC522 based clone.
